# Fritzing sketch TrichromySaturation (saved by Fritzing 0.9.2b)
breadboards: 1

parts:
  Raspberry_Pi1 = Raspberry Pi 2
  S1 = Pushbutton [package="[THT]"]
  SENSOR1 = TCS34725 RGB Color Sensor
  R1 = Resistor [tolerance=±5% resistance=10k package="2512 [SMD]"]
  R2 = Resistor [tolerance=±5% resistance=560 package="1206 [SMD]"]
  R3 = Resistor [tolerance=±5% resistance=560 package="1206 [SMD]"]
  R4 = Resistor [tolerance=±5% resistance=560 package="1206 [SMD]"]
  LED1 = smd LED [color="Blue (430nm)" package="0805 [SMD]"]
  LED2 = smd LED [color="Green (555nm)" package="0805 [SMD]"]
  LED3 = smd LED [color="Red (633nm)" package="0805 [SMD]"]

nets (from the breadboard view):
  N1: Raspberry_Pi1.GPIO2, SENSOR1.SDA
  N2: Raspberry_Pi1.GPIO3, SENSOR1.SCL
  N3: Raspberry_Pi1.GPIO4, S1.Pin_3, S1.Pin_4, R1.Pin_1
  GND: Raspberry_Pi1.GND, S1.Pin_1, S1.Pin_2, SENSOR1.GND, LED1.cathode, LED2.cathode, LED3.cathode
  N4: Raspberry_Pi1.GPIO17, R4.Pin_0
  N5: Raspberry_Pi1.GPIO27, R3.Pin_0
  N6: Raspberry_Pi1.GPIO22, R2.Pin_0
  N7: Raspberry_Pi1.GPIO5, SENSOR1.LED
  5V: Raspberry_Pi1.5V, SENSOR1.VDD, R1.Pin_0
  N8: R2.Pin_1, LED1.anode
  N9: R3.Pin_1, LED2.anode
  N10: R4.Pin_1, LED3.anode

custom parts:
  TCS34725 RGB Color Sensor: TCS34725 RGB Color Sensor with LED
